// Logisim project ledscreens.circ as structural Verilog: 1 circuit, main circuit main
module main (
);

  wire clock_1_out, counter_1_carry;
  wire [4:0] buffer_1_out, buffer_2_out, buffer_3_out, buffer_4_out, buffer_5_out, buffer_6_out,
       buffer_7_out, counter_1_q;
  wire [7:0] counter_2_q;
  wire [31:0] decoder_1_out31, dotmatrix_1_p1;

  Clock clock_1 (.out(clock_1_out));
  Counter #(.max('h1f), .width(5)) counter_1 (
    .clr(1'b0), .load(1'b0), .up(1'b1), .count(1'b1), .clk(clock_1_out), .D({5{1'b0}}),
    .carry(counter_1_carry), .Q(counter_1_q));
  Decoder #(.select(5)) decoder_1 (
    .out0(decoder_1_out31[31]), .out1(decoder_1_out31[30]), .out2(decoder_1_out31[29]),
    .out3(decoder_1_out31[28]), .out4(decoder_1_out31[27]), .out5(decoder_1_out31[26]),
    .out6(decoder_1_out31[25]), .out7(decoder_1_out31[24]), .out8(decoder_1_out31[23]),
    .out9(decoder_1_out31[22]), .out10(decoder_1_out31[21]), .out11(decoder_1_out31[20]),
    .out12(decoder_1_out31[19]), .out13(decoder_1_out31[18]), .out14(decoder_1_out31[17]),
    .out15(decoder_1_out31[16]), .out16(decoder_1_out31[15]), .out17(decoder_1_out31[14]),
    .out18(decoder_1_out31[13]), .out19(decoder_1_out31[12]), .out20(decoder_1_out31[11]),
    .out21(decoder_1_out31[10]), .out22(decoder_1_out31[9]), .out23(decoder_1_out31[8]),
    .out24(decoder_1_out31[7]), .out25(decoder_1_out31[6]), .out26(decoder_1_out31[5]),
    .out27(decoder_1_out31[4]), .out28(decoder_1_out31[3]), .out29(decoder_1_out31[2]),
    .out30(decoder_1_out31[1]), .out31(decoder_1_out31[0]), .sel(buffer_1_out), .en(1'b1));
  assign buffer_1_out = buffer_3_out;  // Buffer buffer_1, 5 bits wide
  assign buffer_2_out = counter_1_q;  // Buffer buffer_2, 5 bits wide
  assign buffer_3_out = buffer_5_out;  // Buffer buffer_3, 5 bits wide
  assign buffer_4_out = buffer_2_out;  // Buffer buffer_4, 5 bits wide
  assign buffer_5_out = buffer_7_out;  // Buffer buffer_5, 5 bits wide
  assign buffer_6_out = buffer_4_out;  // Buffer buffer_6, 5 bits wide
  assign buffer_7_out = buffer_6_out;  // Buffer buffer_7, 5 bits wide
  // DotMatrix #(.inputtype("select"), .matrixcols(32), .matrixrows(32), .persist(64)) dotmatrix_1: pin names not known; wires that end beside it: dotmatrix_1_p1, decoder_1_out31
  Counter counter_2 (
    .clr(1'b0), .load(1'b0), .up(1'b1), .count(1'b1), .clk(counter_1_carry), .D({8{1'b0}}), .Q(counter_2_q));  // open: carry
  ROM #(.addrWidth(13), .dataWidth(32)) rom_1 (.addr({counter_2_q, counter_1_q}), .data(dotmatrix_1_p1));

  // Notes on the sheet:
  //   contents of rom_1 (hex, n*v repeats v):
  //   10*0 1000804 1000800 1000800 1c64a24 1292944 1211884 1292944 1c64a24 24*0 1000804 1000804 e 1424a24
  //   290004 1001884 290004 1424a24 a 22*0 14 8 8 3e 5*8 14 22 20*0 44 28 10 10 fe 5*10 28 44 82 18*0 a0
  //   110 a0 40 40 3f8 5*40 a0 110 208 404 16*0 40 a0 110 a0 40 40 7fc 5*40 a0 110 208 404 16*0 80 140 220
  //   140 1080 880 7e0 90 88 80 80 80 140 220 410 808 16*0 80 140 220 940 880 480 3e0 90 88 80 80 80 140
  //   220 410 808 16*0 80 140 220 1140 880 480 3e0 90 88 80 80 80 140 220 410 808 16*0 80 140 220 940 880
  //   480 3e0 90 88 80 80 80 140 220 410 808 16*0 3c80 4140 8220 10940 20880 480 3e0 90 88 80 80 80 140
  //   220 410 808 16*0 3c80 4140 8220 10140 20080 80 92403e0 8240490 93c0888 1240080 9240080 80 140 220
  //   410 808 16*0 3c80 4140 8220 2010140 fa0080 2500080 25001c0 e02a0 1102a0 1e0f02a0 102a0 1e1e0080 140
  //   220 410 808 16*0 3c80 4140 8220 10140 20080 80080 801c0 b82a0 802a0 802a0 2a0 80 140 220 410 808
  //   16*0 3c80 4140 8220 10140 20080 40080 401c0 14b602a0 155502a0 95202a0 2a0 1fff0080 1080140 1080220
  //   38c0410 10a0808 3040000 15*0 3c80 4140 8220 10140 220080 200080 5b001c0 aa802a0 a9002a0 a003c2a0
  //   aff802a0 4243c080 7600140 2500220 6200410 808 16*0 3c80 4140 8220 10140 220080 200080 2b001c0
  //   2a802a0 11082a0 5801c2a0 aff882a0 a9200080 1200140 3b00220 1280410 3100808 16*0 3c80 4140 8220 10140
  //   80 7fc0080 40401c0 4*40402a0 7fc0080 400140 1f00220 410 808 16*0 3c80 4140 8220 f10140 1080080
  //   1080080 10381c0 8002a0 4382a0 4002a0 4002a0 80 400140 220 410 808 1424*0 3c80 4140 8220 10140 20080
  //   80 1c0 4*2a0 80 140 220 410 808
endmodule
